// Logisim project Marcos_Guerreiro_Multiplicador.circ as structural Verilog: 6 circuits, main circuit 8 BIT MULT
module XOR (
  input  A,
  input  B,
  output out_3
);

  wire and_1_out, and_2_out, not_1_out, not_2_out;

  not not_1 (not_1_out, B);
  not not_2 (not_2_out, A);
  and and_1 (and_1_out, A, not_1_out);
  and and_2 (and_2_out, not_2_out, B);
  or or_1 (out_3, and_1_out, and_2_out);
endmodule

module XNOR (
  input  A,
  input  B,
  output out_3
);

  wire xor_1_out_3;

  XOR xor_1 (.A(A), .B(B), .out_3(xor_1_out_3));
  not not_1 (out_3, xor_1_out_3);
endmodule

module _1_BIT_Hald_Adder (
  input  A,
  input  B,
  output C_OUT,
  output R
);

  and and_1 (C_OUT, A, B);
  XOR xor_1 (.A(A), .B(B), .out_3(R));
endmodule

module _1_BIT_Full_Adder (
  input  A,
  input  B,
  input  C_IN,
  output C_OUT,
  output R
);

  wire and_1_out, and_2_out, and_3_out, or_1_out, xor_1_out_3;

  XOR xor_1 (.A(A), .B(B), .out_3(xor_1_out_3));
  and and_1 (and_1_out, A, B);
  and and_2 (and_2_out, A, C_IN);
  and and_3 (and_3_out, B, C_IN);
  or or_1 (or_1_out, and_1_out, and_2_out);
  XOR xor_2 (.A(xor_1_out_3), .B(C_IN), .out_3(R));
  or or_2 (C_OUT, or_1_out, and_3_out);
endmodule

module _8_BIT_Adder (
  input  [8:0] A,
  input  [8:0] B,
  output [8:0] R,
  output C_OUT
);

  wire n1_bit_full_adder_1_c_out, n1_bit_full_adder_2_c_out, n1_bit_full_adder_3_c_out,
       n1_bit_full_adder_4_c_out, n1_bit_full_adder_5_c_out, n1_bit_full_adder_6_c_out,
       n1_bit_full_adder_7_c_out, n1_bit_full_adder_8_c_out;

  _1_BIT_Full_Adder u_1_bit_full_adder_1 (.A(A[0]), .B(B[0]), .C_IN(1'b0), .C_OUT(n1_bit_full_adder_1_c_out), .R(R[0]));
  _1_BIT_Full_Adder u_1_bit_full_adder_2 (
    .A(A[1]), .B(B[1]), .C_IN(n1_bit_full_adder_1_c_out), .C_OUT(n1_bit_full_adder_2_c_out), .R(R[1]));
  _1_BIT_Full_Adder u_1_bit_full_adder_3 (
    .A(A[2]), .B(B[2]), .C_IN(n1_bit_full_adder_2_c_out), .C_OUT(n1_bit_full_adder_3_c_out), .R(R[2]));
  _1_BIT_Full_Adder u_1_bit_full_adder_4 (
    .A(A[3]), .B(B[3]), .C_IN(n1_bit_full_adder_3_c_out), .C_OUT(n1_bit_full_adder_4_c_out), .R(R[3]));
  _1_BIT_Full_Adder u_1_bit_full_adder_5 (
    .A(A[4]), .B(B[4]), .C_IN(n1_bit_full_adder_4_c_out), .C_OUT(n1_bit_full_adder_5_c_out), .R(R[4]));
  _1_BIT_Full_Adder u_1_bit_full_adder_6 (
    .A(A[5]), .B(B[5]), .C_IN(n1_bit_full_adder_5_c_out), .C_OUT(n1_bit_full_adder_6_c_out), .R(R[5]));
  _1_BIT_Full_Adder u_1_bit_full_adder_7 (
    .A(A[6]), .B(B[6]), .C_IN(n1_bit_full_adder_6_c_out), .C_OUT(n1_bit_full_adder_7_c_out), .R(R[6]));
  _1_BIT_Full_Adder u_1_bit_full_adder_8 (
    .A(A[7]), .B(B[7]), .C_IN(n1_bit_full_adder_7_c_out), .C_OUT(n1_bit_full_adder_8_c_out), .R(R[7]));
  _1_BIT_Full_Adder u_1_bit_full_adder_9 (
    .A(A[8]), .B(B[8]), .C_IN(n1_bit_full_adder_8_c_out), .C_OUT(C_OUT), .R(R[8]));
endmodule

module _8_BIT_MULT (
  input  [7:0] M,
  input  [7:0] Q,
  output [15:0] RESULT
);

  wire [8:0] and_1_out, and_2_out, and_3_out, and_4_out, and_5_out, and_6_out, and_7_out, and_8_out;
  wire [8:1] n8_bit_adder_1_r, n8_bit_adder_2_r, n8_bit_adder_3_r, n8_bit_adder_4_r, n8_bit_adder_5_r,
       n8_bit_adder_6_r;
  wire [8:8] n8_bit_adder_1_c_out, n8_bit_adder_2_c_out, n8_bit_adder_3_c_out, n8_bit_adder_4_c_out,
       n8_bit_adder_5_c_out, n8_bit_adder_6_c_out;

  assign and_1_out = {1'b0, M} & {9{Q[0]}};  // AND_Gate and_1, 9 bits wide
  assign and_2_out = {M, 1'b0} & {9{Q[1]}};  // AND_Gate and_2, 9 bits wide
  assign and_3_out = {9{Q[2]}} & {M, 1'b0};  // AND_Gate and_3, 9 bits wide
  assign and_4_out = {9{Q[3]}} & {M, 1'b0};  // AND_Gate and_4, 9 bits wide
  assign and_5_out = {9{Q[4]}} & {M, 1'b0};  // AND_Gate and_5, 9 bits wide
  assign and_6_out = {9{Q[5]}} & {M, 1'b0};  // AND_Gate and_6, 9 bits wide
  assign and_7_out = {9{Q[6]}} & {M, 1'b0};  // AND_Gate and_7, 9 bits wide
  assign and_8_out = {9{Q[7]}} & {M, 1'b0};  // AND_Gate and_8, 9 bits wide
  _8_BIT_Adder u_8_bit_adder_1 (
    .A(and_1_out), .B(and_2_out), .R({n8_bit_adder_1_r, RESULT[0]}), .C_OUT(n8_bit_adder_1_c_out[8]));
  _8_BIT_Adder u_8_bit_adder_2 (
    .A({n8_bit_adder_1_c_out[8], n8_bit_adder_1_r}), .B(and_3_out), .R({n8_bit_adder_2_r, RESULT[1]}),
    .C_OUT(n8_bit_adder_2_c_out[8]));
  _8_BIT_Adder u_8_bit_adder_3 (
    .A({n8_bit_adder_2_c_out[8], n8_bit_adder_2_r}), .B(and_4_out), .R({n8_bit_adder_3_r, RESULT[2]}),
    .C_OUT(n8_bit_adder_3_c_out[8]));
  _8_BIT_Adder u_8_bit_adder_4 (
    .A({n8_bit_adder_3_c_out[8], n8_bit_adder_3_r}), .B(and_5_out), .R({n8_bit_adder_4_r, RESULT[3]}),
    .C_OUT(n8_bit_adder_4_c_out[8]));
  _8_BIT_Adder u_8_bit_adder_5 (
    .A({n8_bit_adder_4_c_out[8], n8_bit_adder_4_r}), .B(and_6_out), .R({n8_bit_adder_5_r, RESULT[4]}),
    .C_OUT(n8_bit_adder_5_c_out[8]));
  _8_BIT_Adder u_8_bit_adder_6 (
    .A({n8_bit_adder_5_c_out[8], n8_bit_adder_5_r}), .B(and_7_out), .R({n8_bit_adder_6_r, RESULT[5]}),
    .C_OUT(n8_bit_adder_6_c_out[8]));
  _8_BIT_Adder u_8_bit_adder_7 (
    .A({n8_bit_adder_6_c_out[8], n8_bit_adder_6_r}), .B(and_8_out), .R(RESULT[14:6]), .C_OUT(RESULT[15]));
endmodule
