// Logisim project TP1-Marcos.circ as structural Verilog: 16 circuits, main circuit main
module main (
  output IO_s,
  output IO_e,
  output data_address,
  output input_output
);

  wire flags_1_b_s, flags_1_equal_s, flags_1_larger_s, flags_1_zero_s, or_1_out, uc_1_acc_e, uc_1_acc_s,
       uc_1_bus1, uc_1_flags_s, uc_1_iar_e, uc_1_iar_s, uc_1_ir_set, uc_1_mar_s, uc_1_r0_e, uc_1_r0_s,
       uc_1_r1_e, uc_1_r1_s, uc_1_r2_e, uc_1_r2_s, uc_1_r3_e, uc_1_r3_s, uc_1_ram_e, uc_1_ram_s, uc_1_tmp_s,
       ula_1_a_larger, ula_1_carry_out, ula_1_equal, ula_1_zero;
  wire [2:0] uc_1_ula_op;
  wire [7:0] acc_1_out_4, bus1_1_out_3, ir_1_out_3, mar_1_out_3, tmp_1_out_3, ula_1_c;

  ULA ula_1 (
    .A(acc_1_out_4), .B(bus1_1_out_3), .C(ula_1_c), .in_1(uc_1_ula_op), .carry_out(ula_1_carry_out),
    .a_larger(ula_1_a_larger), .equal(ula_1_equal), .zero(ula_1_zero));  // open: carry_in
  ACC acc_1 (.in_1(ula_1_c), .out_4(acc_1_out_4), .s_ACC(uc_1_acc_s), .e_ACC(uc_1_acc_e));
  // Probe on bus1_1_out_3
  TMP tmp_1 (.in_1(acc_1_out_4), .out_3(tmp_1_out_3), .set(uc_1_tmp_s));
  bus1 bus1_1 (.in_1(tmp_1_out_3), .out_3(bus1_1_out_3), .bus_1(uc_1_bus1));
  Flags flags_1 (
    .B_e(ula_1_carry_out), .larger_e(ula_1_a_larger), .equal_e(ula_1_equal), .zero_e(ula_1_zero),
    .B_s(flags_1_b_s), .larger_s(flags_1_larger_s), .equal_s(flags_1_equal_s), .zero_s(flags_1_zero_s),
    .set(uc_1_flags_s));
  // Probe on acc_1_out_4
  R R0 (.in_1(acc_1_out_4), .set(uc_1_r0_s), .enable(uc_1_r0_e), .out_4(acc_1_out_4));
  UC uc_1 (
    .ULA_op(uc_1_ula_op), .from_carry_out(flags_1_b_s), .from_larger(flags_1_larger_s),
    .from_equal(flags_1_equal_s), .from_zero(flags_1_zero_s), .Flags_s(uc_1_flags_s), .bus1(uc_1_bus1),
    .TMP_s(uc_1_tmp_s), .R0_s(uc_1_r0_s), .R0_e(uc_1_r0_e), .R1_s(uc_1_r1_s), .R1_e(uc_1_r1_e),
    .R2_s(uc_1_r2_s), .R2_e(uc_1_r2_e), .R3_s(uc_1_r3_s), .R3_e(uc_1_r3_e), .MAR_s(uc_1_mar_s),
    .ACC_s(uc_1_acc_s), .ACC_e(uc_1_acc_e), .IAR_s(uc_1_iar_s), .IAR_e(uc_1_iar_e), .IR_input(ir_1_out_3),
    .IR_set(uc_1_ir_set), .Input_Output(input_output), .Data_Address(data_address), .IO_e(IO_e), .IO_s(IO_s),
    .RAM_e(uc_1_ram_e), .RAM_s(uc_1_ram_s));
  IAR iar_1 (.in_3(acc_1_out_4), .set(uc_1_iar_s), .enable(uc_1_iar_e), .out_4(acc_1_out_4));
  R R1 (.in_1(acc_1_out_4), .set(uc_1_r1_s), .enable(uc_1_r1_e), .out_4(acc_1_out_4));
  IR ir_1 (.out_3(ir_1_out_3), .set(uc_1_ir_set), .in_2(acc_1_out_4));
  R R2 (.in_1(acc_1_out_4), .set(uc_1_r2_s), .enable(uc_1_r2_e), .out_4(acc_1_out_4));
  R R3 (.in_1(acc_1_out_4), .set(uc_1_r3_s), .enable(uc_1_r3_e), .out_4(acc_1_out_4));
  MAR mar_1 (.in_1(acc_1_out_4), .set(uc_1_mar_s), .out_3(mar_1_out_3));
  // Probe on mar_1_out_3
  RAM #(.databus("bidir"), .\type ("nonvolatile")) ram_1 (
    .addr(mar_1_out_3), .we(uc_1_ram_s), .oe(uc_1_ram_e), .clk(or_1_out), .data(acc_1_out_4));
  or or_1 (or_1_out, uc_1_ram_e, uc_1_ram_s);
  // Probe on acc_1_out_4
endmodule

module clk_main (
  output clk_s,
  output clk_e,
  output clk_o
);

  wire clk_d_out;

  Clock #(.highDuration(2), .lowDuration(2)) clk (.out(clk_o));
  Clock #(.highDuration(2), .lowDuration(2), .phaseOffset(3)) clk_d (.out(clk_d_out));
  or or_1 (clk_e, clk_o, clk_d_out);
  and and_1 (clk_s, clk_o, clk_d_out);
endmodule

module stepper (
  input  clk_o,
  output s1,
  output s2,
  output s3,
  output s4,
  output s5,
  output s6
);

  wire [2:0] counter_1_q;

  Counter #(.max('h7), .width(3)) counter_1 (
    .D(3'b000), .Q(counter_1_q), .clk(clk_o));  // open: load, count, carry, up, clr
  Decoder #(.disabled("Z"), .enable("false"), .select(3)) decoder_1 (
    .out1(s1), .out2(s2), .out3(s3), .out4(s4), .out5(s5), .out6(s6), .sel(counter_1_q));  // open: out0, out7
endmodule

// CONTROL
module UC (
  input  from_carry_out,
  input  from_larger,
  input  from_equal,
  input  from_zero,
  input  [7:0] IR_input,
  output bus1,
  output TMP_s,
  output R0_s,
  output R0_e,
  output R1_s,
  output R1_e,
  output R2_s,
  output R2_e,
  output R3_s,
  output R3_e,
  output MAR_s,
  output [2:0] ULA_op,
  output Flags_s,
  output ACC_s,
  output ACC_e,
  output IAR_s,
  output IAR_e,
  output IR_set,
  output Input_Output,
  output Data_Address,
  output IO_e,
  output IO_s,
  output RAM_e,
  output RAM_s
);

  wire A_out, and_5_out, and_6_out, and_7_out, and_8_out, and_9_out, and_10_out, and_11_out, and_12_out,
       and_16_out, and_17_out, and_18_out, and_19_out, and_20_out, and_21_out, and_22_out, and_23_out,
       and_24_out, and_25_out, and_26_out, and_27_out, and_28_out, and_29_out, and_30_out, and_31_out,
       and_32_out, and_33_out, and_34_out, and_35_out, and_36_out, and_37_out, and_38_out, and_39_out,
       and_40_out, and_41_out, and_42_out, and_43_out, C_out, Clock_clk_e, Clock_clk_o, Clock_clk_s,
       decoder_1_out0, decoder_1_out1, decoder_1_out2, decoder_1_out3, decoder_2_out0, decoder_2_out1,
       decoder_2_out2, decoder_2_out3, decoder_3_out0, decoder_3_out1, decoder_3_out2, decoder_3_out3,
       decoder_3_out4, decoder_3_out5, decoder_3_out6, decoder_3_out7, decoder_4_out0, decoder_4_out1,
       decoder_4_out2, decoder_4_out3, E_out, not_1_out, not_2_out, not_3_out, or_6_out, or_7_out, or_8_out,
       or_9_out, or_10_out, or_11_out, or_12_out, or_13_out, or_14_out, or_15_out, or_16_out, stepper_1_s1,
       stepper_1_s2, stepper_1_s3, stepper_1_s4, stepper_1_s5, stepper_1_s6, Z_out;

  or or_1 (R0_e, and_5_out, and_9_out);
  or or_2 (R1_e, and_6_out, and_10_out);
  or or_3 (R2_e, and_7_out, and_11_out);
  or or_4 (R3_e, and_8_out, and_12_out);
  clk_main Clock (.clk_s(Clock_clk_s), .clk_e(Clock_clk_e), .clk_o(Clock_clk_o));
  and and_1 (IAR_e, or_6_out, Clock_clk_e);
  and and_2 (RAM_e, or_7_out, Clock_clk_e);
  and and_3 (ACC_e, or_8_out, Clock_clk_e);
  and and_4 (IO_e, and_40_out, Clock_clk_e);
  and and_5 (and_5_out, Clock_clk_e, or_9_out, decoder_1_out0);
  and and_6 (and_6_out, Clock_clk_e, or_9_out, decoder_1_out1);
  and and_7 (and_7_out, Clock_clk_e, or_9_out, decoder_1_out2);
  and and_8 (and_8_out, Clock_clk_e, or_9_out, decoder_1_out3);
  and and_9 (and_9_out, Clock_clk_e, or_10_out, decoder_2_out0);
  and and_10 (and_10_out, Clock_clk_e, or_10_out, decoder_2_out1);
  and and_11 (and_11_out, Clock_clk_e, or_10_out, decoder_2_out2);
  and and_12 (and_12_out, Clock_clk_e, or_10_out, decoder_2_out3);
  Decoder #(.enable("false"), .select(2)) decoder_1 (
    .out0(decoder_1_out0), .out1(decoder_1_out1), .out2(decoder_1_out2), .out3(decoder_1_out3),
    .sel(IR_input[1:0]));
  Decoder #(.enable("false"), .select(2)) decoder_2 (
    .out0(decoder_2_out0), .out1(decoder_2_out1), .out2(decoder_2_out2), .out3(decoder_2_out3),
    .sel(IR_input[3:2]));
  or or_5 (bus1, stepper_1_s1, and_32_out, and_31_out, and_28_out);
  or or_6 (or_6_out, stepper_1_s1, and_28_out, and_30_out, and_31_out);
  or or_7 (or_7_out, stepper_1_s2, and_43_out, and_37_out, and_35_out);
  or or_8 (or_8_out, stepper_1_s3, and_39_out, and_42_out, and_41_out);
  or or_9 (or_9_out, and_25_out, and_36_out, and_29_out, and_33_out);
  or or_10 (or_10_out, and_27_out, and_26_out, and_34_out);
  and and_13 (ULA_op[0], stepper_1_s5, IR_input[7], IR_input[4]);
  and and_14 (ULA_op[1], stepper_1_s5, IR_input[7], IR_input[5]);
  and and_15 (ULA_op[2], stepper_1_s5, IR_input[7], IR_input[6]);
  Decoder #(.enable("false"), .select(3)) decoder_3 (
    .out0(decoder_3_out0), .out1(decoder_3_out1), .out2(decoder_3_out2), .out3(decoder_3_out3),
    .out4(decoder_3_out4), .out5(decoder_3_out5), .out6(decoder_3_out6), .out7(decoder_3_out7),
    .sel(IR_input[6:4]));
  not not_1 (not_1_out, IR_input[7]);
  and and_16 (and_16_out, not_1_out, decoder_3_out0);
  and and_17 (and_17_out, not_1_out, decoder_3_out1);
  and and_18 (and_18_out, not_1_out, decoder_3_out2);
  and and_19 (and_19_out, not_1_out, decoder_3_out3);
  and and_20 (and_20_out, not_1_out, decoder_3_out4);
  and and_21 (and_21_out, not_1_out, decoder_3_out5);
  and and_22 (and_22_out, not_1_out, decoder_3_out6);
  and and_23 (and_23_out, not_1_out, decoder_3_out7);
  and and_24 (and_24_out, IR_input[4], IR_input[5], IR_input[6]);
  not not_2 (not_2_out, and_24_out);
  and and_25 (and_25_out, stepper_1_s4, IR_input[7]);
  and and_26 (and_26_out, stepper_1_s4, and_16_out);
  and and_27 (and_27_out, stepper_1_s4, and_17_out);
  and and_28 (and_28_out, stepper_1_s4, and_18_out);
  and and_29 (and_29_out, stepper_1_s4, and_19_out);
  and and_30 (and_30_out, stepper_1_s4, and_20_out);
  and and_31 (and_31_out, stepper_1_s4, and_21_out);
  and and_32 (and_32_out, stepper_1_s4, and_22_out);
  and and_33 (and_33_out, stepper_1_s4, and_23_out, IR_input[3]);
  stepper stepper_1 (
    .clk_o(Clock_clk_o), .s1(stepper_1_s1), .s2(stepper_1_s2), .s3(stepper_1_s3), .s4(stepper_1_s4),
    .s5(stepper_1_s5), .s6(stepper_1_s6));
  not not_3 (not_3_out, IR_input[3]);
  and C (C_out, IR_input[3], from_carry_out);
  and A (A_out, IR_input[2], from_larger);
  and E (E_out, IR_input[1], from_equal);
  and Z (Z_out, IR_input[0], from_zero);
  and and_34 (and_34_out, stepper_1_s5, IR_input[7]);
  and and_35 (and_35_out, stepper_1_s5, and_16_out);
  and and_36 (and_36_out, stepper_1_s5, and_17_out);
  and and_37 (and_37_out, stepper_1_s5, and_18_out);
  and and_38 (and_38_out, stepper_1_s5, and_20_out);
  and and_39 (and_39_out, stepper_1_s5, and_21_out);
  and and_40 (and_40_out, stepper_1_s5, and_23_out, not_3_out);
  or or_11 (or_11_out, C_out, A_out, E_out, Z_out);
  and and_41 (and_41_out, stepper_1_s6, IR_input[7], not_2_out);
  and and_42 (and_42_out, stepper_1_s6, and_18_out);
  and and_43 (and_43_out, stepper_1_s6, and_21_out, or_11_out);
  or or_12 (or_12_out, and_35_out, and_41_out, and_37_out, and_40_out);
  or or_13 (or_13_out, stepper_1_s1, and_28_out, and_31_out, and_26_out, and_27_out, and_30_out);
  or or_14 (or_14_out, stepper_1_s3, and_29_out, and_38_out, and_39_out, and_42_out, and_43_out);
  or or_15 (or_15_out, stepper_1_s1, and_28_out, and_32_out, and_34_out);
  or or_16 (or_16_out, and_32_out, and_34_out);
  Decoder #(.enable("false"), .select(2)) decoder_4 (
    .out0(decoder_4_out0), .out1(decoder_4_out1), .out2(decoder_4_out2), .out3(decoder_4_out3),
    .sel(IR_input[1:0]));
  and and_44 (IR_set, Clock_clk_s, stepper_1_s2);
  and and_45 (MAR_s, Clock_clk_s, or_13_out);
  and and_46 (IAR_s, Clock_clk_s, or_14_out);
  and and_47 (ACC_s, Clock_clk_s, or_15_out);
  and and_48 (RAM_s, Clock_clk_s, and_36_out);
  and and_49 (TMP_s, Clock_clk_s, and_25_out);
  and and_50 (Flags_s, Clock_clk_s, or_16_out);
  and and_51 (IO_s, Clock_clk_s, and_33_out);
  and and_52 (R0_s, Clock_clk_s, or_12_out, decoder_4_out0);
  and and_53 (R1_s, Clock_clk_s, or_12_out, decoder_4_out1);
  and and_54 (R2_s, Clock_clk_s, or_12_out, decoder_4_out2);
  and and_55 (R3_s, Clock_clk_s, or_12_out, decoder_4_out3);

  assign Data_Address = IR_input[2];
  assign Input_Output = IR_input[3];

  // Other names for the same wires on the sheet: from_IR[7:0] = IR_input; ULA[2:0] = ULA_op
endmodule

module TMP (
  input  [7:0] in_1,
  input  set,
  output [7:0] out_3
);

  Register register_1 (.D(in_1), .Q(out_3), .clk(set));  // open: en, clr
endmodule

module R (
  input  [7:0] in_1,
  input  set,
  input  enable,
  output [7:0] out_4
);

  wire [7:0] register_1_q;

  Register register_1 (.D(in_1), .Q(register_1_q), .clk(set));  // open: en, clr
  assign out_4 = enable ? register_1_q : 8'bz;  // Controlled_Buffer controlled_buffer_1
endmodule

module ULA (
  input  [2:0] in_1,
  input  [7:0] A,
  input  [7:0] B,
  input  carry_in,
  output carry_out,
  output [7:0] C,
  output a_larger,
  output equal,
  output zero
);

  wire adder_1_cout, shl_1_carry_out, shr_1_out_3;
  wire [7:0] adder_1_out, and_1_out, not_1_out, or_1_out, shl_1_out_2, shr_1_out_2, xor_1_out;

  Comparator comparator_1 (.a(A), .b(B), .gt(a_larger), .eq(equal));  // open: lt
  Adder adder_1 (.a(A), .b(B), .out(adder_1_out), .cin(carry_in), .cout(adder_1_cout));
  SHR shr_1 (.in_1(A), .out_3(shr_1_out_3), .out_2(shr_1_out_2));
  SHL shl_1 (.in_1(A), .carry_out(shl_1_carry_out), .out_2(shl_1_out_2));
  assign not_1_out = ~A;  // NOT_Gate not_1, 8 bits wide
  assign and_1_out = A & B;  // AND_Gate and_1, 8 bits wide
  assign or_1_out = A | B;  // OR_Gate or_1, 8 bits wide
  assign xor_1_out = A ^ B;  // XOR_Gate xor_1, 8 bits wide
  selector selector_1 (
    .ADD_carry_in(adder_1_cout), .SHR_carry_in(shr_1_out_3), .SHL_carry_out(shl_1_carry_out), .OP_in(in_1),
    .carry_out(carry_out));
  Multiplexer #(.enable("false"), .select(3), .width(8)) multiplexer_1 (
    .in0(adder_1_out), .in1(shr_1_out_2), .in2(shl_1_out_2), .in3(not_1_out), .in4(and_1_out),
    .in5(or_1_out), .in6(xor_1_out), .in7(A), .out(C), .sel(in_1));
  Comparator comparator_2 (.a(C), .b({8{1'b0}}), .eq(zero));  // open: gt, lt

  // Other names for the same wires on the sheet: op[2:0] = in_1
endmodule

// Flag
module Flags (
  input  B_e,
  input  larger_e,
  input  equal_e,
  input  set,
  input  zero_e,
  output B_s,
  output larger_s,
  output equal_s,
  output zero_s
);

  Register #(.width(4)) register_1 (
    .D({zero_e, equal_e, larger_e, B_e}), .Q({zero_s, equal_s, larger_s, B_s}), .clk(set));  // open: en, clr
endmodule

module ACC (
  input  [7:0] in_1,
  input  s_ACC,
  input  e_ACC,
  output [7:0] out_4
);

  wire [7:0] register_1_q;

  Register register_1 (.D(in_1), .Q(register_1_q), .clk(s_ACC));  // open: en, clr
  assign out_4 = e_ACC ? register_1_q : 8'bz;  // Controlled_Buffer controlled_buffer_1
endmodule

module IR (
  input  set,
  input  [7:0] in_2,
  output [7:0] out_3
);

  Register register_1 (.D(in_2), .Q(out_3), .clk(set));  // open: en, clr
endmodule

// BUS
module bus1 (
  input  [7:0] in_1,
  input  bus_1,
  output [7:0] out_3
);

  wire not_1_out;

  and and_1 (out_3[7], in_1[7], not_1_out);
  and and_2 (out_3[6], in_1[6], not_1_out);
  and and_3 (out_3[5], in_1[5], not_1_out);
  and and_4 (out_3[4], in_1[4], not_1_out);
  and and_5 (out_3[3], in_1[3], not_1_out);
  and and_6 (out_3[2], in_1[2], not_1_out);
  and and_7 (out_3[1], in_1[1], not_1_out);
  or or_1 (out_3[0], in_1[0], bus_1);
  not not_1 (not_1_out, bus_1);
endmodule

module SHR (
  input  [7:0] in_1,
  output [7:0] out_2,
  output out_3
);


  assign out_2 = {{2{in_1[7]}}, in_1[6:1]};
  assign out_3 = in_1[0];
endmodule

module SHL (
  input  [7:0] in_1,
  output [7:0] out_2,
  output carry_out
);


  assign carry_out = in_1[7];
  assign out_2 = {in_1[6:0], 1'b0};
endmodule

// SEL
module selector (
  input  ADD_carry_in,
  input  SHR_carry_in,
  input  SHL_carry_out,
  input  [2:0] OP_in,
  output carry_out
);

  wire and_1_out, and_2_out, and_3_out, not_1_out, not_2_out, not_3_out, not_4_out, not_5_out, not_6_out,
       not_7_out;

  not not_1 (not_1_out, OP_in[2]);
  and and_1 (and_1_out, ADD_carry_in, not_1_out, not_2_out, not_3_out);
  not not_2 (not_2_out, OP_in[1]);
  not not_3 (not_3_out, OP_in[0]);
  not not_4 (not_4_out, OP_in[2]);
  and and_2 (and_2_out, SHR_carry_in, not_4_out, not_5_out, OP_in[0]);
  not not_5 (not_5_out, OP_in[1]);
  not not_6 (not_6_out, OP_in[2]);
  and and_3 (and_3_out, SHL_carry_out, not_6_out, OP_in[1], not_7_out);
  not not_7 (not_7_out, OP_in[0]);
  or or_1 (carry_out, and_1_out, and_2_out, and_3_out);
endmodule

module IAR (
  input  set,
  input  enable,
  input  [7:0] in_3,
  output [7:0] out_4
);

  wire [7:0] register_1_q;

  Register register_1 (.D(in_3), .Q(register_1_q), .clk(set));  // open: en, clr
  assign out_4 = enable ? register_1_q : 8'bz;  // Controlled_Buffer controlled_buffer_1
endmodule

module MAR (
  input  [7:0] in_1,
  input  set,
  output [7:0] out_3
);

  Register register_1 (.D(in_1), .Q(out_3), .clk(set));  // open: en, clr
endmodule
